# Fritzing sketch drink_meter_board (saved by Fritzing 0.9.9b)
circuit board: 9.5cm x 7.2cm
breadboards: 1

parts:
  X1 = USB Connectors [package=usb-microb]
  U1 = 74HC595 [package="DIP16 [THT]"]
  PIC16F1938 = PICAXE-28 [package=THT]
  C1 = Ceramic Capacitor [capacitance=100nF voltage=35V package="100 mil [THT, multilayer]"]
  J2 = female pin header, 2 pins [form="♀ (female)"]
  R1 = Resistor [tolerance=±5% power=0.25 resistance=220 package=THT]
  R2 = Resistor [tolerance=±5% power=0.25 resistance=220 package=THT]
  J3 = female pin header, 2 pins [form="♀ (female)"]
  J4 = female pin header, 2 pins [form="♀ (female)"]
  R3 = Resistor [tolerance=±5% power=0.25 resistance=220 package=THT]
  J6 = double row female pin header, 20 pins [form="♀ (female)"]
  R4 = Resistor [tolerance=±5% power=0.25 resistance=220 package=THT]
  R5 = Resistor [tolerance=±5% power=0.25 resistance=220 package=THT]
  R6 = Resistor [tolerance=±5% power=0.25 resistance=220 package=THT]
  R7 = Resistor [tolerance=±5% power=0.25 resistance=220 package=THT]
  R8 = Resistor [tolerance=±5% power=0.25 resistance=220 package=THT]
  R9 = Resistor [tolerance=±5% power=0.25 resistance=220 package=THT]
  R10 = Resistor [tolerance=±5% power=0.25 resistance=220 package=THT]
  R11 = Resistor [tolerance=±5% power=0.25 resistance=220 package=THT]
  R12 = Resistor [tolerance=±5% power=0.25 resistance=220 package=THT]
  R13 = Resistor [tolerance=±5% power=0.25 resistance=220 package=THT]
  LCD = female pin header, 4 pins [form="♀ (female)"]
  TM1637 = female pin header, 4 pins [form="♀ (female)"]
  HX711 = female pin header, 4 pins [form="♀ (female)"]

nets:
  GND: X1.GND, U1.GND, U1.OE, PIC16F1938.0V, C1.0, J2.pin1, J3.pin1, J4.pin1, J6.pin11, J6.pin12, J6.pin13, J6.pin14, J6.pin15, J6.pin16, J6.pin17, J6.pin18, J6.pin19, J6.pin20, LCD.pin1, TM1637.pin4, HX711.pin4
  N1: X1.VBUS, U1.MR, U1.VCC, PIC16F1938.+V, C1.1, R1.Pin_0, R2.Pin_0, R3.Pin_1, LCD.pin2, TM1637.pin3, HX711.pin3
  N2: U1.Q1, R5.Pin_1
  N3: U1.Q2, R6.Pin_1
  N4: U1.Q3, R7.Pin_1
  N5: U1.Q4, R8.Pin_1
  N6: U1.Q5, R9.Pin_1
  N7: U1.Q6, R10.Pin_1
  N8: U1.Q7, R11.Pin_1
  N9: U1.SH_CP, PIC16F1938.Out_7
  N10: U1.ST_CP, PIC16F1938.Out_6
  N11: U1.DS, PIC16F1938.Out_5
  N12: U1.Q0, R4.Pin_1
  N13: PIC16F1938.In_A0, R12.Pin_1
  N14: PIC16F1938.In_A1, R13.Pin_1
  N15: PIC16F1938.In_3, LCD.pin3
  N16: PIC16F1938.In_4, LCD.pin4
  N17: PIC16F1938.In_5, J2.pin2, R1.Pin_1
  N18: PIC16F1938.In_6, R2.Pin_1, J3.pin2
  N19: PIC16F1938.In_7, J4.pin2, R3.Pin_0
  N20: PIC16F1938.Out_1, HX711.pin2
  N21: PIC16F1938.Out_2, HX711.pin1
  N22: PIC16F1938.Out_3, TM1637.pin2
  N23: PIC16F1938.Out_4, TM1637.pin1
  N24: J6.pin1, R13.Pin_0
  N25: J6.pin2, R12.Pin_0
  N26: J6.pin3, R11.Pin_0
  N27: J6.pin4, R10.Pin_0
  N28: J6.pin5, R9.Pin_0
  N29: J6.pin6, R8.Pin_0
  N30: J6.pin7, R7.Pin_0
  N31: J6.pin8, R6.Pin_0
  N32: J6.pin9, R5.Pin_0
  N33: J6.pin10, R4.Pin_0
