# Fritzing sketch drink_meter_v2 (saved by Fritzing 0.9.9b)
circuit board: 8.46667cm x 5.64444cm
breadboards: 1

parts:
  PIC16F1938 = PICAXE-28A [package=THT]
  DC = Power plug
  C1 = Ceramic Capacitor [capacitance=100nF voltage=35V package="100 mil [THT, multilayer]"]
  LCD = female pin header, 4 pins [form="♀ (female)"]
  SW1 = female pin header, 2 pins [form="♀ (female)"]
  R1 = Resistor [tolerance=±5% power=0.25 resistance=220 package=THT]
  R2 = Resistor [tolerance=±5% power=0.25 resistance=220 package=THT]
  SW2 = female pin header, 2 pins [form="♀ (female)"]
  R3 = Resistor [tolerance=±5% power=0.25 resistance=220 package=THT]
  SW3 = female pin header, 2 pins [form="♀ (female)"]
  HX711 = female pin header, 4 pins [form="♀ (female)"]
  TM1637 = female pin header, 4 pins [form="♀ (female)"]
  U74HC595 = 74HC595 [package="DIP16 [THT]"]
  LED_ARRAY = double row female pin header, 20 pins [form="♀ (female)"]
  R4 = Resistor [tolerance=±5% power=0.25 resistance=220 package=THT]
  R5 = Resistor [tolerance=±5% power=0.25 resistance=220 package=THT]
  R6 = Resistor [tolerance=±5% power=0.25 resistance=220 package=THT]
  R7 = Resistor [tolerance=±5% power=0.25 resistance=220 package=THT]
  R8 = Resistor [tolerance=±5% power=0.25 resistance=220 package=THT]
  R9 = Resistor [tolerance=±5% power=0.25 resistance=220 package=THT]
  R10 = Resistor [tolerance=±5% power=0.25 resistance=220 package=THT]
  R11 = Resistor [tolerance=±5% power=0.25 resistance=220 package=THT]
  R12 = Resistor [tolerance=±5% power=0.25 resistance=220 package=THT]
  R13 = Resistor [tolerance=±5% power=0.25 resistance=220 package=THT]

nets:
  N1: PIC16F1938.In_A0, R12.Pin_1
  N2: PIC16F1938.In_A1, R13.Pin_1
  GND: PIC16F1938.0V, DC.GND, C1.0, LCD.pin1, SW1.pin1, SW2.pin1, SW3.pin1, HX711.pin4, TM1637.pin4, U74HC595.GND, U74HC595.OE, LED_ARRAY.pin1, LED_ARRAY.pin2, LED_ARRAY.pin3, LED_ARRAY.pin4, LED_ARRAY.pin5, LED_ARRAY.pin6, LED_ARRAY.pin7, LED_ARRAY.pin8, LED_ARRAY.pin9, LED_ARRAY.pin10
  N3: PIC16F1938.In_3, LCD.pin3
  N4: PIC16F1938.In_4, LCD.pin4
  N5: PIC16F1938.In_5, SW1.pin2, R1.Pin_0
  N6: PIC16F1938.In_6, R2.Pin_0, SW2.pin2
  N7: PIC16F1938.In_7, R3.Pin_0, SW3.pin2
  VCC: PIC16F1938.+V, DC.VCC, C1.1, LCD.pin2, R1.Pin_1, R2.Pin_1, R3.Pin_1, HX711.pin3, TM1637.pin3, U74HC595.MR, U74HC595.VCC
  N8: PIC16F1938.Out_1, HX711.pin2
  N9: PIC16F1938.Out_2, HX711.pin1
  N10: PIC16F1938.Out_3, TM1637.pin2
  N11: PIC16F1938.Out_4, TM1637.pin1
  N12: PIC16F1938.Out_5, U74HC595.DS
  N13: PIC16F1938.Out_6, U74HC595.ST_CP
  N14: PIC16F1938.Out_7, U74HC595.SH_CP
  N15: U74HC595.Q1, R5.Pin_1
  N16: U74HC595.Q2, R6.Pin_1
  N17: U74HC595.Q3, R7.Pin_1
  N18: U74HC595.Q4, R8.Pin_1
  N19: U74HC595.Q5, R9.Pin_1
  N20: U74HC595.Q6, R10.Pin_1
  N21: U74HC595.Q7, R11.Pin_1
  N22: U74HC595.Q0, R4.Pin_1
  N23: LED_ARRAY.pin11, R13.Pin_0
  N24: LED_ARRAY.pin12, R12.Pin_0
  N25: LED_ARRAY.pin13, R11.Pin_0
  N26: LED_ARRAY.pin14, R10.Pin_0
  N27: LED_ARRAY.pin15, R9.Pin_0
  N28: LED_ARRAY.pin16, R8.Pin_0
  N29: LED_ARRAY.pin17, R7.Pin_0
  N30: LED_ARRAY.pin18, R6.Pin_0
  N31: LED_ARRAY.pin19, R5.Pin_0
  N32: LED_ARRAY.pin20, R4.Pin_0

notes:
  Drink Meter v.1.0
